// Logisim project 16-bitALU (datapath).circ as structural Verilog: 4 circuits, main circuit main
module main (
  input  [15:0] A,
  input  [15:0] B,
  input  [2:0] OP,
  output zero,
  output [15:0] Result,
  output overflow,
  output Cout
);

  wire Ain, Bin, Cin;
  wire [3:0] bit_extender_1_out;
  wire [15:0] adder_subtracter_1_result, And_out, multiplexer_1_out, multiplexer_2_out, Nor_out, not_1_out,
       not_2_out, Or_out, shifter_1_out, shifter_2_out;

  assign not_1_out = ~B;  // NOT_Gate not_1, 16 bits wide
  Multiplexer #(.width(16)) multiplexer_1 (.in0(A), .in1(not_2_out), .out(multiplexer_1_out), .sel(Ain));  // open: en
  assign not_2_out = ~A;  // NOT_Gate not_2, 16 bits wide
  Multiplexer #(.width(16)) multiplexer_2 (.in0(B), .in1(not_1_out), .out(multiplexer_2_out), .sel(Bin));  // open: en
  Bit_Extender #(.in_width(16), .out_width(4)) bit_extender_1 (.in(multiplexer_2_out), .out(bit_extender_1_out));
  Adder_Subtracter adder_subtracter_1 (
    .C_in(Cin), .Input_A(multiplexer_1_out), .Input_B(B), .Result(adder_subtracter_1_result),
    .Overflow(overflow), .Cout(Cout), .Binvert(Bin));
  assign And_out = multiplexer_1_out & multiplexer_2_out;  // AND_Gate And, 16 bits wide
  assign Or_out = multiplexer_1_out | multiplexer_2_out;  // OR_Gate Or, 16 bits wide
  Shifter #(.width(16)) shifter_1 (.in(multiplexer_1_out), .\dist (bit_extender_1_out), .out(shifter_1_out));
  Shifter #(.width(16), .shift("lr")) shifter_2 (
    .in(multiplexer_1_out), .\dist (bit_extender_1_out), .out(shifter_2_out));
  assign Nor_out = multiplexer_1_out & multiplexer_2_out;  // AND_Gate Nor, 16 bits wide
  Multiplexer #(.select(3), .width(16)) multiplexer_3 (
    .in0(And_out), .in1(Or_out), .in2(adder_subtracter_1_result), .in3(adder_subtracter_1_result),
    .in4(shifter_1_out), .in5(shifter_2_out), .in6(Nor_out), .out(Result), .sel(OP));  // open: in7, en
  Invert invert_1 (.I2(OP[2]), .Ain(Ain), .I1(OP[1]), .Bin(Bin), .I0(OP[0]), .Cin(Cin));
  nor nor_2 (zero, Result[0], Result[1], Result[2], Result[3], Result[4], Result[5], Result[6], Result[7], Result[8], Result[9], Result[10], Result[11], Result[12], Result[13], Result[14], Result[15]);

  // Notes on the sheet:
  //   Instruction
  //   and
  //   nor
  //   OP
  //   000
  //   001
  //   or
  //   add
  //   010
  //   sub
  //   011
  //   100
  //   sll
  //   srl
  //   101
  //   110
  //   sll
  //   srl
  //   Add
  //   sub
endmodule

module Adder_Subtracter (
  input  C_in,
  input  [15:0] Input_A,
  input  [15:0] Input_B,
  input  Binvert,
  output [15:0] Result,
  output Overflow,
  output Cout
);

  wire adder_1_cout, adder_2_cout, adder_3_cout, adder_4_cout, adder_5_cout, adder_6_cout, adder_7_cout,
       adder_8_cout, adder_9_cout, adder_10_cout, adder_11_cout, adder_12_cout, adder_13_cout, adder_14_cout,
       adder_15_cout, b0, b1, b2, b3, b4, b5, b6, b7, b8, b9, b10, b11, b12, b13, b14, b15;
  wire [15:0] not_1_out;

  assign not_1_out = ~Input_B;  // NOT_Gate not_1, 16 bits wide
  Multiplexer #(.width(16)) multiplexer_1 (
    .in0(Input_B), .in1(not_1_out),
    .out({b15, b14, b13, b12, b11, b10, b9, b8, b7, b6, b5, b4, b3, b2, b1, b0}), .sel(Binvert));  // open: en
  Adder #(.width(1)) adder_1 (.a(Input_A[0]), .b(b0), .out(Result[0]), .cin(C_in), .cout(adder_1_cout));
  Adder #(.width(1)) adder_2 (.a(Input_A[1]), .b(b1), .out(Result[1]), .cin(adder_1_cout), .cout(adder_2_cout));
  Adder #(.width(1)) adder_3 (.a(Input_A[2]), .b(b2), .out(Result[2]), .cin(adder_2_cout), .cout(adder_3_cout));
  Adder #(.width(1)) adder_4 (.a(Input_A[3]), .b(b3), .out(Result[3]), .cin(adder_3_cout), .cout(adder_4_cout));
  Adder #(.width(1)) adder_5 (.a(Input_A[4]), .b(b4), .out(Result[4]), .cin(adder_4_cout), .cout(adder_5_cout));
  Adder #(.width(1)) adder_6 (.a(Input_A[5]), .b(b5), .out(Result[5]), .cin(adder_5_cout), .cout(adder_6_cout));
  Adder #(.width(1)) adder_7 (.a(Input_A[6]), .b(b6), .out(Result[6]), .cin(adder_6_cout), .cout(adder_7_cout));
  Adder #(.width(1)) adder_8 (.a(Input_A[7]), .b(b7), .out(Result[7]), .cin(adder_7_cout), .cout(adder_8_cout));
  Adder #(.width(1)) adder_9 (.a(Input_A[8]), .b(b8), .out(Result[8]), .cin(adder_8_cout), .cout(adder_9_cout));
  Adder #(.width(1)) adder_10 (.a(Input_A[9]), .b(b9), .out(Result[9]), .cin(adder_9_cout), .cout(adder_10_cout));
  Adder #(.width(1)) adder_11 (.a(Input_A[10]), .b(b10), .out(Result[10]), .cin(adder_10_cout), .cout(adder_11_cout));
  Adder #(.width(1)) adder_12 (.a(Input_A[11]), .b(b11), .out(Result[11]), .cin(adder_11_cout), .cout(adder_12_cout));
  Adder #(.width(1)) adder_13 (.a(Input_A[12]), .b(b12), .out(Result[12]), .cin(adder_12_cout), .cout(adder_13_cout));
  Adder #(.width(1)) adder_14 (.a(Input_A[13]), .b(b13), .out(Result[13]), .cin(adder_13_cout), .cout(adder_14_cout));
  Adder #(.width(1)) adder_15 (.a(Input_A[14]), .b(b14), .out(Result[14]), .cin(adder_14_cout), .cout(adder_15_cout));
  Adder #(.width(1)) adder_16 (.a(Input_A[15]), .b(b15), .out(Result[15]), .cin(adder_15_cout), .cout(Cout));
  xor xor_1 (Overflow, adder_15_cout, Cout);

  // Other names for the same wires on the sheet: a0 = Input_A[0]; a1 = Input_A[1]; a2 = Input_A[2]; a3 = Input_A[3];
  //   a4 = Input_A[4]; a5 = Input_A[5]; a6 = Input_A[6]; a7 = Input_A[7]; a8 = Input_A[8]; a9 = Input_A[9];
  //   a10 = Input_A[10]; a11 = Input_A[11]; a12 = Input_A[12]; a13 = Input_A[13]; a14 = Input_A[14];
  //   a15 = Input_A[15]
endmodule

module Test (
  input  in_1,
  input  [15:0] in_2,
  input  [15:0] in_3,
  input  [2:0] in_4,
  input  in_5,
  input  in_6,
  output [15:0] out_7,
  output out_8,
  output out_9,
  output out_10
);

  // main main_1: pin names not known; wires that end beside it: in_1, in_2, in_3, in_5, in_6, in_4, out_7, out_8, out_9, out_10
endmodule

module Invert (
  input  I2,
  input  I1,
  input  I0,
  output Ain,
  output Bin,
  output Cin
);

  wire and_2_out, and_3_out, not_1_out, not_2_out, not_3_out, not_4_out;

  not not_1 (not_1_out, I0);
  not not_2 (not_2_out, I2);
  not not_3 (not_3_out, I0);
  not not_4 (not_4_out, I2);
  and and_1 (Ain, I2, I1, not_1_out);
  and and_2 (and_2_out, not_2_out, I1, I0);
  and and_3 (and_3_out, I2, I1, not_3_out);
  and and_4 (Cin, not_4_out, I1, I0);
  or or_1 (Bin, and_2_out, and_3_out);
endmodule
