// Logisim project CSE 332 lab 3 new.circ as structural Verilog: 1 circuit, main circuit main
module main (
  input  in_1,
  input  I4,
  input  I3,
  input  in_4,
  input  in_5,
  input  i1,
  input  [1:0] S1_S0,
  input  in_8,
  output A4,
  output A3,
  output A2,
  output A1
);

  wire clock_1_out, multiplexer_1_out, multiplexer_2_out, multiplexer_3_out, multiplexer_4_out;

  Multiplexer #(.select(2)) multiplexer_1 (
    .in0(A4), .in1(in_1), .in2(A3), .in3(I4), .out(multiplexer_1_out), .sel(S1_S0));  // open: en
  Multiplexer #(.select(2)) multiplexer_2 (
    .in0(A3), .in1(A4), .in2(A2), .in3(I3), .out(multiplexer_2_out), .sel(S1_S0));  // open: en
  Multiplexer #(.select(2)) multiplexer_3 (
    .in0(A2), .in1(A3), .in2(A1), .in3(in_4), .out(multiplexer_3_out), .sel(S1_S0));  // open: en
  Multiplexer #(.select(2)) multiplexer_4 (
    .in0(A1), .in1(A2), .in2(in_5), .in3(i1), .out(multiplexer_4_out), .sel(S1_S0));  // open: en
  Clock clock_1 (.out(clock_1_out));
  D_Flip_Flop d_ff_1 (.clk(clock_1_out), .D(multiplexer_1_out), .Q(A4), .reset(in_8));  // open: Qn, preset, en
  D_Flip_Flop d_ff_2 (.clk(clock_1_out), .D(multiplexer_2_out), .Q(A3), .reset(in_8));  // open: Qn, preset, en
  D_Flip_Flop d_ff_3 (.clk(clock_1_out), .D(multiplexer_3_out), .Q(A2), .reset(in_8));  // open: Qn, preset, en
  D_Flip_Flop d_ff_4 (.clk(clock_1_out), .D(multiplexer_4_out), .Q(A1), .reset(in_8));  // open: Qn, preset, en

  // Notes on the sheet:
  //   shift right
  //   shift left
  //   i2
  //   1931804042
  //   PARINDA RAHMAN
endmodule
