// Logisim project CSE 332 lab4.circ as structural Verilog: 1 circuit, main circuit main
module main (
  input  UP,
  input  DOWN,
  input  in_3,
  output A0,
  output A1,
  output A2,
  output A3,
  output A4
);

  wire and_1_out, and_2_out, and_3_out, and_4_out, and_5_out, and_6_out, and_7_out, and_8_out, and_9_out,
       clock_1_out, d_ff_1_qn, d_ff_2_qn, d_ff_3_qn, d_ff_4_qn, not_1_out, or_1_out, or_2_out, or_3_out,
       or_4_out, or_5_out, xor_1_out, xor_2_out, xor_3_out, xor_4_out, xor_5_out;

  not not_1 (not_1_out, UP);
  and and_1 (and_1_out, not_1_out, DOWN);
  and and_2 (and_2_out, and_1_out, d_ff_1_qn);
  and and_3 (and_3_out, UP, A0);
  and and_4 (and_4_out, and_2_out, d_ff_2_qn);
  and and_5 (and_5_out, and_3_out, A1);
  and and_6 (and_6_out, and_5_out, A2);
  and and_7 (and_7_out, and_4_out, d_ff_3_qn);
  and and_8 (and_8_out, and_6_out, A3);
  and and_9 (and_9_out, and_7_out, d_ff_4_qn);
  or or_1 (or_1_out, and_6_out, and_7_out);
  or or_2 (or_2_out, and_8_out, and_9_out);
  or or_3 (or_3_out, UP, and_1_out);
  or or_4 (or_4_out, and_3_out, and_2_out);
  or or_5 (or_5_out, and_5_out, and_4_out);
  xor xor_1 (xor_1_out, A0, or_3_out);
  xor xor_2 (xor_2_out, A1, or_4_out);
  xor xor_3 (xor_3_out, A2, or_5_out);
  xor xor_4 (xor_4_out, A3, or_1_out);
  xor xor_5 (xor_5_out, A4, or_2_out);
  Clock clock_1 (.out(clock_1_out));
  D_Flip_Flop d_ff_1 (.clk(clock_1_out), .D(xor_1_out), .Q(A0), .Qn(d_ff_1_qn), .reset(in_3));  // open: preset, en
  D_Flip_Flop d_ff_2 (.clk(clock_1_out), .D(xor_2_out), .Q(A1), .Qn(d_ff_2_qn), .reset(in_3));  // open: preset, en
  D_Flip_Flop d_ff_3 (.clk(clock_1_out), .D(xor_3_out), .Q(A2), .Qn(d_ff_3_qn), .reset(in_3));  // open: preset, en
  D_Flip_Flop d_ff_4 (.clk(clock_1_out), .D(xor_4_out), .Q(A3), .Qn(d_ff_4_qn), .reset(in_3));  // open: preset, en
  D_Flip_Flop d_ff_5 (.clk(clock_1_out), .D(xor_5_out), .Q(A4), .reset(in_3));  // open: Qn, preset, en
endmodule
