// Logisim project CSE332 Lab3.circ as structural Verilog: 1 circuit, main circuit main
module main (
  input  Clear,
  input  I4,
  input  i3,
  input  I2,
  input  I1,
  input  in_6,
  input  [1:0] S1S0,
  input  in_8,
  output A4,
  output A3,
  output A2,
  output A1
);

  wire clock_1_out, multiplexer_2_out, multiplexer_3_out, multiplexer_4_out, not_1_out, undriven;

  Clock clock_1 (.out(clock_1_out));
  Multiplexer #(.select(2)) multiplexer_1 (.in0(A4), .in1(A3), .in2(in_6), .in3(I4), .sel(S1S0));  // open: out, en
  not not_1 (not_1_out, Clear);
  D_Flip_Flop d_ff_1 (.clk(clock_1_out), .Q(A4), .reset(not_1_out));  // open: D, Qn, preset, en
  Multiplexer #(.select(2)) multiplexer_2 (
    .in0(A3), .in1(A4), .in2(A2), .in3(i3), .out(multiplexer_2_out), .sel(S1S0));  // open: en
  D_Flip_Flop d_ff_2 (
    .clk(clock_1_out), .D(multiplexer_2_out), .Q(A3), .preset(undriven), .en(undriven), .reset(not_1_out));  // open: Qn
  Multiplexer #(.select(2)) multiplexer_3 (
    .in0(A2), .in1(A3), .in2(A1), .in3(I2), .out(multiplexer_3_out), .sel(S1S0));  // open: en
  D_Flip_Flop d_ff_3 (.clk(clock_1_out), .D(multiplexer_3_out), .Q(A2), .reset(not_1_out));  // open: Qn, preset, en
  Multiplexer #(.select(2)) multiplexer_4 (
    .in0(A1), .in1(A2), .in2(in_8), .in3(I1), .out(multiplexer_4_out), .sel(S1S0));  // open: en
  D_Flip_Flop d_ff_4 (.clk(clock_1_out), .D(multiplexer_4_out), .Q(A1), .reset(not_1_out));  // open: Qn, preset, en

  // Notes on the sheet:
  //   Serial Input for shift right
  //   Serial input for shift left
endmodule
