// Logisim project CSE332 lab 7.circ as structural Verilog: 4 circuits, main circuit main
module main (
  input  in_1,
  input  in_2,
  output [3:0] out_3,
  output [15:0] out_4,
  output [15:0] out_5,
  output [3:0] out_6,
  output out_7,
  output out_8,
  output out_9,
  output [15:0] out_10
);

  wire Clk_out;
  wire [1:0] bit_extender_1_out;
  wire [3:0] Opcode, Rs;
  wire [7:0] adder_1_out, register_1_q;

  Clock Clk (.out(Clk_out));
  Register register_1 (.D(adder_1_out), .Q(register_1_q), .clk(Clk_out), .clr(in_2));  // open: en
  Adder adder_1 (.a(8'h1), .b(register_1_q), .out(adder_1_out));  // open: cin, cout
  ROM #(.dataWidth(16)) rom_1 (.addr(register_1_q), .data({Opcode, Rs, out_3, out_6}));  // open: sel
  CSE_332_lab_5_main main_1 (
    .in_1(out_4), .in_2(Rs), .in_3(out_6), .READ_REGISTER_2(out_3), .out_6(out_5), .out_7(out_10),
    .in_5(Clk_out));
  Bit_Extender #(.in_width(4), .out_width(2)) bit_extender_1 (.in(Opcode), .out(bit_extender_1_out));
  // _16_bit_ALU 16_bit_alu_1: pin names not known; wires that end beside it: in_1, bit_extender_1_out, out_5, out_10, out_4, out_7, out_8, out_9

  // Other names for the same wires on the sheet: RD[3:0] = out_6; Rt[3:0] = out_3; Result[15:0] = out_4

  // Notes on the sheet:
  //   R Type 
  //   contents of rom_1 (hex, n*v repeats v):
  //   2123 124 2345
endmodule

module i_type (
  input  in_1,
  input  clear,
  output [15:0] out_3,
  output out_4,
  output out_5,
  output out_6
);

  wire Clk_out;
  wire [1:0] bit_extender_1_out;
  wire [3:0] Opcode, Rd, rom_1_data, Rs, undriven;
  wire [7:0] adder_1_out, register_1_q;
  wire [15:0] bit_extender_2_out, main_1_out_6, main_1_out_7;

  Clock Clk (.out(Clk_out));
  Register register_1 (.D(adder_1_out), .Q(register_1_q), .clk(Clk_out), .clr(clear));  // open: en
  Adder adder_1 (.a(8'h1), .b(register_1_q), .out(adder_1_out));  // open: cin, cout
  ROM #(.dataWidth(16)) rom_1 (.addr(register_1_q), .data({Opcode, Rs, Rd, rom_1_data}));  // open: sel
  CSE_332_lab_5_main main_1 (
    .in_1(out_3), .in_2(Rs), .in_3(Rd), .READ_REGISTER_2(undriven), .out_6(main_1_out_6),
    .out_7(main_1_out_7), .in_5(Clk_out));
  Bit_Extender #(.in_width(4), .out_width(2)) bit_extender_1 (.in(Opcode), .out(bit_extender_1_out));
  assign bit_extender_2_out = {{12{1'b0}}, rom_1_data};  // Bit_Extender bit_extender_2
  // _16_bit_ALU 16_bit_alu_1: pin names not known; wires that end beside it: in_1, bit_extender_1_out, main_1_out_6, bit_extender_2_out, out_3, out_4, out_5, out_6

  // Other names for the same wires on the sheet: Result[15:0] = out_3
endmodule

module J_Type (
  input  in_1,
  input  in_2,
  input  in_3,
  output [3:0] out_4,
  output [15:0] out_5,
  output [15:0] out_6,
  output [3:0] out_7,
  output [15:0] out_8,
  output [3:0] out_9,
  output out_10,
  output out_11,
  output out_12,
  output [15:0] out_13,
  output [11:0] out_14,
  output [3:0] out_15
);

  wire Clk_out;
  wire [1:0] bit_extender_1_out;
  wire [3:0] multiplexer_2_out;
  wire [11:0] adder_1_out, multiplexer_1_out, register_1_q;
  wire [15:0] ID, main_1_out_7;

  Clock Clk (.out(Clk_out));
  Multiplexer #(.width(12)) multiplexer_1 (
    .in0(12'h1), .in1({out_8[11:8], out_4, out_7}), .out(multiplexer_1_out), .sel(in_2));  // open: en
  Register #(.width(12)) register_1 (.D(adder_1_out), .Q(register_1_q), .clk(Clk_out), .clr(in_3));  // open: en
  Adder #(.width(12)) adder_1 (.a(multiplexer_1_out), .b(register_1_q), .out(adder_1_out));  // open: cin, cout
  Multiplexer #(.width(4)) multiplexer_2 (
    .in0(out_7), .in1(out_4), .out(multiplexer_2_out), .sel(out_8[14]));  // open: en
  ROM #(.addrWidth(12), .dataWidth(16)) rom_1 (.addr(register_1_q), .data({out_8[15:8], out_4, out_7}));  // open: sel
  CSE_332_lab_5_main main_1 (
    .in_1(out_5), .in_2(out_8[11:8]), .in_3(multiplexer_2_out), .READ_REGISTER_2(out_4), .out_6(out_6),
    .out_7(main_1_out_7), .in_5(Clk_out));
  Bit_Extender #(.in_width(4), .out_width(2)) bit_extender_1 (.in(out_8[15:12]), .out(bit_extender_1_out));
  Multiplexer #(.width(16)) multiplexer_3 (.in0(main_1_out_7), .in1(ID), .out(out_13), .sel(out_8[14]));  // open: en
  // _16_bit_ALU 16_bit_alu_1: pin names not known; wires that end beside it: in_1, bit_extender_1_out, out_6, out_13, out_5, out_10, out_11, out_12, out_7
  assign ID = {{12{1'b0}}, out_7};  // Bit_Extender bit_extender_2

  assign out_8[7:0] = {out_4, out_7};
  assign out_9 = out_8[15:12];
  assign out_14 = {out_8[11:8], out_4, out_7};
  assign out_15 = out_8[15:12];

  // Other names for the same wires on the sheet: Opcode[3:0] = out_8[15:12]; Result[15:0] = out_5; RD[3:0] = out_7;
  //   Target[11:0] = {out_8[11:8], out_4, out_7}; Rt[3:0] = out_4; Rs[3:0] = out_8[11:8]

  // Notes on the sheet:
  //   R Type 
  //   contents of rom_1 (hex, n*v repeats v):
  //   2123 124 2345
endmodule

module Merge_I_Type_and_R_Type (
  input  in_1,
  input  in_2,
  output [3:0] out_3,
  output [15:0] out_4,
  output [15:0] out_5,
  output [3:0] out_6,
  output [15:0] out_7,
  output [3:0] out_8,
  output out_9,
  output out_10,
  output out_11,
  output [15:0] out_12,
  output [3:0] out_13
);

  wire Clk_out;
  wire [1:0] bit_extender_1_out;
  wire [3:0] multiplexer_1_out;
  wire [7:0] adder_1_out, register_1_q;
  wire [15:0] ID, main_1_out_7;

  Clock Clk (.out(Clk_out));
  Register register_1 (.D(adder_1_out), .Q(register_1_q), .clk(Clk_out), .clr(in_2));  // open: en
  Adder adder_1 (.a(8'h1), .b(register_1_q), .out(adder_1_out));  // open: cin, cout
  Multiplexer #(.width(4)) multiplexer_1 (
    .in0(out_6), .in1(out_3), .out(multiplexer_1_out), .sel(out_7[14]));  // open: en
  ROM #(.dataWidth(16)) rom_1 (.addr(register_1_q), .data({out_7[15:8], out_3, out_6}));  // open: sel
  CSE_332_lab_5_main main_1 (
    .in_1(out_4), .in_2(out_7[11:8]), .in_3(multiplexer_1_out), .READ_REGISTER_2(out_3), .out_6(out_5),
    .out_7(main_1_out_7), .in_5(Clk_out));
  Bit_Extender #(.in_width(4), .out_width(2)) bit_extender_1 (.in(out_7[15:12]), .out(bit_extender_1_out));
  Multiplexer #(.width(16)) multiplexer_2 (.in0(main_1_out_7), .in1(ID), .out(out_12), .sel(out_7[14]));  // open: en
  // _16_bit_ALU 16_bit_alu_1: pin names not known; wires that end beside it: in_1, bit_extender_1_out, out_5, out_12, out_4, out_9, out_10, out_11
  assign ID = {{12{1'b0}}, out_6};  // Bit_Extender bit_extender_2

  assign out_7[7:0] = {out_3, out_6};
  assign out_8 = out_7[15:12];
  assign out_13 = out_7[15:12];

  // Other names for the same wires on the sheet: RD[3:0] = out_6; Rt[3:0] = out_3; Rs[3:0] = out_7[11:8];
  //   Opcode[3:0] = out_7[15:12]; Result[15:0] = out_4

  // Notes on the sheet:
  //   R Type 
  //   contents of rom_1 (hex, n*v repeats v):
  //   2123 124 2345
endmodule
