// Logisim project CSE332 lab7 new.circ as structural Verilog: 2 circuits, main circuit main
module main (
  input  [15:0] in_1,
  input  in_2,
  output [15:0] out_3,
  output out_4,
  output out_5,
  output out_6
);

  wire clock_1_out, n16_bit_alu_1_p3, n16_bit_alu_1_p4;
  wire [1:0] bit_extender_1_out;

  Clock clock_1 (.out(clock_1_out));
  Bit_Extender #(.in_width(4), .out_width(2)) bit_extender_1 (.in(in_1[15:12]), .out(bit_extender_1_out));
  // _16_bit_ALU 16_bit_alu_1: pin names not known; wires that end beside it: in_2, bit_extender_1_out, n16_bit_alu_1_p3, n16_bit_alu_1_p4, out_3, out_4, out_5, out_6

  // Other names for the same wires on the sheet: RD[3:0] = in_1[3:0]; Rt[3:0] = in_1[7:4]; Rs[3:0] = in_1[11:8];
  //   Opcode[3:0] = in_1[15:12]; Result[15:0] = out_3
endmodule

module I_Type (
  input  [15:0] in_1,
  input  in_2,
  output [15:0] out_3,
  output out_4,
  output out_5,
  output out_6
);

  wire clock_1_out, n16_bit_alu_1_p1, n16_bit_alu_1_p4;
  wire [1:0] bit_extender_1_out;
  wire [15:0] bit_extender_2_out;

  Clock clock_1 (.out(clock_1_out));
  Bit_Extender #(.in_width(4), .out_width(2)) bit_extender_1 (.in(in_1[15:12]), .out(bit_extender_1_out));
  assign bit_extender_2_out = {{12{1'b0}}, in_1[3:0]};  // Bit_Extender bit_extender_2
  // _16_bit_ALU 16_bit_alu_1: pin names not known; wires that end beside it: n16_bit_alu_1_p1, in_2, bit_extender_1_out, n16_bit_alu_1_p4, bit_extender_2_out, out_3, out_4, out_5, out_6

  // Other names for the same wires on the sheet: RD[3:0] = in_1[7:4]; Rs[3:0] = in_1[11:8]; Opcode[3:0] = in_1[15:12];
  //   Result[15:0] = out_3
endmodule
