// Logisim project Control-unit.circ as structural Verilog: 2 circuits, main circuit main
module main (
  input  [3:0] OPCode,
  output out_2,
  output out_3,
  output out_4,
  output out_5,
  output out_6,
  output out_7,
  output out_8,
  output out_9,
  output [2:0] out_10,
  output out_11
);

  Control_Unit control_unit_1 (
    .Op4(OPCode[3]), .Op3(OPCode[2]), .Op2(OPCode[1]), .Op1(OPCode[0]), .RegDst(out_2), .ALUSrc(out_3),
    .MemToReg(out_4), .RegWrite(out_5), .MemRead(out_6), .MemWrite(out_7), .BranchBne(out_8),
    .BranchBeq(out_9), .ALUOp2(out_10[2]), .ALUOp1(out_10[1]), .ALUOp0(out_10[0]), .Jump(out_11));
endmodule

module Control_Unit (
  input  Op4,
  input  Op3,
  input  Op2,
  input  Op1,
  output RegDst,
  output ALUSrc,
  output MemToReg,
  output RegWrite,
  output MemRead,
  output MemWrite,
  output BranchBne,
  output BranchBeq,
  output ALUOp2,
  output ALUOp1,
  output ALUOp0,
  output Jump
);

  wire and_1_out, and_2_out, and_3_out, and_4_out, and_5_out, and_7_out, and_8_out, and_9_out, and_10_out,
       and_12_out, and_13_out, and_14_out, and_15_out, and_18_out, and_19_out, and_20_out, and_21_out,
       and_22_out, and_23_out, and_24_out, and_25_out, not_1_out, not_2_out, not_3_out, not_4_out, not_5_out,
       not_6_out, not_7_out, not_8_out, not_9_out, not_10_out, not_11_out, not_12_out, not_13_out,
       not_14_out, not_15_out, not_16_out, not_17_out, not_18_out, not_19_out, not_20_out, not_21_out,
       not_22_out, not_23_out, not_24_out, not_25_out, not_26_out, not_27_out, not_28_out, not_29_out,
       not_30_out, not_31_out, not_32_out, not_33_out, not_34_out, not_35_out, not_36_out, not_37_out,
       not_38_out, not_39_out, not_40_out;

  not not_1 (not_1_out, Op4);
  and and_1 (and_1_out, not_1_out, not_2_out);
  not not_2 (not_2_out, Op3);
  not not_3 (not_3_out, Op4);
  and and_2 (and_2_out, not_3_out, not_4_out);
  not not_4 (not_4_out, Op2);
  not not_5 (not_5_out, Op4);
  and and_3 (and_3_out, not_5_out, not_6_out);
  not not_6 (not_6_out, Op1);
  and and_4 (and_4_out, Op3, Op2, Op1);
  and and_5 (and_5_out, Op4, not_7_out);
  not not_7 (not_7_out, Op3);
  and and_6 (MemToReg, Op4, not_8_out);
  not not_8 (not_8_out, Op3);
  not not_9 (not_9_out, Op4);
  not not_10 (not_10_out, Op3);
  not not_11 (not_11_out, Op2);
  and and_7 (and_7_out, not_10_out, not_11_out, not_12_out);
  not not_12 (not_12_out, Op1);
  not not_13 (not_13_out, Op3);
  and and_8 (and_8_out, not_13_out, Op2, Op1);
  not not_14 (not_14_out, Op3);
  not not_15 (not_15_out, Op2);
  not not_16 (not_16_out, Op1);
  not not_17 (not_17_out, Op3);
  not not_18 (not_18_out, Op3);
  not not_19 (not_19_out, Op2);
  not not_20 (not_20_out, Op3);
  not not_21 (not_21_out, Op1);
  not not_22 (not_22_out, Op2);
  not not_23 (not_23_out, Op2);
  not not_24 (not_24_out, Op1);
  not not_25 (not_25_out, Op4);
  and and_9 (and_9_out, not_25_out, Op3, not_26_out);
  not not_26 (not_26_out, Op2);
  not not_27 (not_27_out, Op4);
  and and_10 (and_10_out, not_27_out, Op3, not_28_out);
  not not_28 (not_28_out, Op1);
  not not_29 (not_29_out, Op3);
  not not_30 (not_30_out, Op2);
  not not_31 (not_31_out, Op2);
  not not_32 (not_32_out, Op1);
  not not_33 (not_33_out, Op4);
  not not_34 (not_34_out, Op3);
  not not_35 (not_35_out, Op2);
  not not_36 (not_36_out, Op4);
  not not_37 (not_37_out, Op3);
  not not_38 (not_38_out, Op4);
  not not_39 (not_39_out, Op1);
  not not_40 (not_40_out, Op2);
  and and_11 (Jump, Op4, Op3, Op2, Op1);
  or or_1 (RegDst, and_1_out, and_2_out, and_3_out);
  or or_2 (ALUSrc, and_4_out, and_5_out);
  or or_3 (RegWrite, not_9_out, and_7_out, and_8_out);
  and and_12 (and_12_out, Op4, not_14_out, not_15_out, not_16_out);
  or or_4 (MemRead, and_12_out, and_13_out);
  and and_13 (and_13_out, Op4, not_17_out, Op2, Op1);
  and and_14 (and_14_out, Op4, not_18_out, not_19_out, Op1);
  or or_5 (MemWrite, and_14_out, and_15_out);
  and and_15 (and_15_out, Op4, not_20_out, Op2, not_21_out);
  and and_16 (BranchBne, Op4, Op3, not_22_out, Op1);
  and and_17 (BranchBeq, Op4, Op3, not_23_out, not_24_out);
  or or_6 (ALUOp2, and_9_out, and_10_out);
  and and_18 (and_18_out, not_29_out, not_30_out);
  and and_19 (and_19_out, not_31_out, not_32_out);
  and and_20 (and_20_out, not_33_out, Op3, Op2, Op1);
  and and_21 (and_21_out, Op4, not_34_out);
  and and_22 (and_22_out, Op4, not_35_out);
  and and_23 (and_23_out, not_36_out, not_37_out, Op1);
  or or_7 (ALUOp0, and_23_out, and_24_out, and_25_out);
  and and_24 (and_24_out, not_38_out, Op3, Op2, not_39_out);
  and and_25 (and_25_out, Op4, Op3, not_40_out);
  or or_8 (ALUOp1, and_18_out, and_19_out, and_20_out, and_21_out, and_22_out);
endmodule
