// Logisim project LAB REPORT 2.circ as structural Verilog: 1 circuit, main circuit main
module main (
  input  A,
  input  in_2,
  input  C,
  output _6
);

  wire and_1_out, and_2_out, not_1_out, not_2_out, not_3_out, or_2_out, or_3_out, or_4_out, or_5_out;

  not not_1 (not_1_out, A);
  not not_2 (not_2_out, in_2);
  not not_3 (not_3_out, C);
  or or_1 (not_1_out, A, not_2_out, not_3_out);
  or or_2 (or_2_out, A, in_2, C);
  or or_3 (or_3_out, not_1_out, in_2, C);
  or or_4 (or_4_out, not_1_out, C, not_3_out);
  or or_5 (or_5_out, not_1_out, not_2_out, not_3_out);
  and and_1 (and_1_out, or_2_out, or_4_out);
  and and_2 (and_2_out, or_5_out, not_1_out, or_3_out);
  and and_3 (_6, and_2_out, and_1_out);

  // Notes on the sheet:
  //   1
  //   B
  //   2
  //   1
  //   2
  //   1
  //   B
  //   A
  //   C'
  //   2
  //   13
  //   B'
  //   12
  //   11
  //   1
  //   2
  //   8
  //   C
  //   A+B+C
  //   A'
  //   B'
  //   C
  //   A
  //   B
  //   9
  //   B
  //   C'
  //   C'
  //   A'
  //   A+B'+C'
  //   10
  //   13
  //   12
  //   11
  //   A'
  //   3
  //   4
  //   5
  //   A'+B+C'
  //   1
  //   2
  //   8
  //   10
  //   A'+B+C
  //   6
  //   A'+B'+C'
  //   9
  //   1
  //   2
  //   (A+B+C)(A'+B+C')
  //   2
  //   13
  //   (A'+B'+C').(A+B'+C')(A+B+C)
  //   1
  //   3
  //   12
  //   4
  //   5
  //   F=(A'+B'+C')(A+B'+C')(A+B+C)(A+B+C)(A'+B+C')
  //   PARINDA RAHMAN
  //                    1931804042
endmodule
