// Logisim project Lab5.circ as structural Verilog: 2 circuits, main circuit main
module main (
  input  [15:0] WriteData,
  input  [15:0] in,
  input  inclk,
  input  RegWrite,
  input  [3:0] WriteReg1,
  input  [3:0] RdReg,
  input  [3:0] WriteReg2,
  input  in_8,
  output [15:0] RdReg1,
  output [15:0] RdReg2
);

  wire and_1_out, and_2_out, and_3_out, and_4_out, and_5_out, and_6_out, and_7_out, and_8_out, and_9_out,
       and_10_out, and_11_out, and_12_out, and_13_out, and_14_out, and_15_out, and_16_out, decoder_1_out0,
       decoder_1_out1, decoder_1_out2, decoder_1_out3, decoder_1_out4, decoder_1_out5, decoder_1_out6,
       decoder_1_out7, decoder_1_out8, decoder_1_out9, decoder_1_out10, decoder_1_out11, decoder_1_out12,
       decoder_1_out13, decoder_1_out14, decoder_1_out15;
  wire [15:0] multiplexer_1_out, register_1_q, register_2_q, register_3_q, register_4_q, register_5_q,
       register_6_q, register_7_q, register_8_q, register_9_q, register_10_q, register_11_q, register_12_q,
       register_13_q, register_14_q, register_15_q, register_16_q, register_17_q;

  Decoder #(.select(4)) decoder_1 (
    .out0(decoder_1_out0), .out1(decoder_1_out1), .out2(decoder_1_out2), .out3(decoder_1_out3),
    .out4(decoder_1_out4), .out5(decoder_1_out5), .out6(decoder_1_out6), .out7(decoder_1_out7),
    .out8(decoder_1_out8), .out9(decoder_1_out9), .out10(decoder_1_out10), .out11(decoder_1_out11),
    .out12(decoder_1_out12), .out13(decoder_1_out13), .out14(decoder_1_out14), .out15(decoder_1_out15),
    .sel(RdReg));  // open: en
  and and_1 (and_1_out, decoder_1_out0, RegWrite);
  and and_2 (and_2_out, decoder_1_out1, RegWrite);
  and and_3 (and_3_out, decoder_1_out2, RegWrite);
  and and_4 (and_4_out, decoder_1_out3, RegWrite);
  and and_5 (and_5_out, decoder_1_out4, RegWrite);
  and and_6 (and_6_out, decoder_1_out5, RegWrite);
  and and_7 (and_7_out, decoder_1_out6, RegWrite);
  and and_8 (and_8_out, decoder_1_out7, RegWrite);
  and and_9 (and_9_out, decoder_1_out8, RegWrite);
  and and_10 (and_10_out, decoder_1_out9, RegWrite);
  and and_11 (and_11_out, decoder_1_out10, RegWrite);
  and and_12 (and_12_out, decoder_1_out11, RegWrite);
  and and_13 (and_13_out, decoder_1_out12, RegWrite);
  and and_14 (and_14_out, decoder_1_out13, RegWrite);
  and and_15 (and_15_out, decoder_1_out14, RegWrite);
  and and_16 (and_16_out, decoder_1_out15, RegWrite);
  Register #(.width(16)) register_1 (.D(multiplexer_1_out), .en(and_1_out), .Q(register_1_q), .clk(in_8));  // open: clr
  Register #(.width(16)) register_2 (.D(WriteData), .en(and_2_out), .Q(register_2_q), .clk(in_8));  // open: clr
  Register #(.width(16)) register_3 (.D(WriteData), .en(and_3_out), .Q(register_3_q), .clk(in_8));  // open: clr
  Register #(.width(16)) register_4 (.D(WriteData), .en(and_4_out), .Q(register_4_q), .clk(in_8));  // open: clr
  Register #(.width(16)) register_5 (.D(WriteData), .en(and_5_out), .Q(register_5_q), .clk(in_8));  // open: clr
  Register #(.width(16)) register_6 (.D(WriteData), .en(and_6_out), .Q(register_6_q), .clk(in_8));  // open: clr
  Register #(.width(16)) register_7 (.D(WriteData), .en(and_7_out), .Q(register_7_q), .clk(in_8));  // open: clr
  Register #(.width(16)) register_8 (.D(WriteData), .en(and_8_out), .Q(register_8_q), .clk(in_8));  // open: clr
  Register #(.width(16)) register_9 (.D(WriteData), .en(and_9_out), .Q(register_9_q), .clk(in_8));  // open: clr
  Register #(.width(16)) register_10 (.D(WriteData), .en(and_10_out), .Q(register_10_q), .clk(in_8));  // open: clr
  Register #(.width(16)) register_11 (.D(WriteData), .en(and_11_out), .Q(register_11_q), .clk(in_8));  // open: clr
  Register #(.width(16)) register_12 (.D(WriteData), .en(and_12_out), .Q(register_12_q), .clk(in_8));  // open: clr
  Register #(.width(16)) register_13 (.D(WriteData), .en(and_13_out), .Q(register_13_q), .clk(in_8));  // open: clr
  Register #(.width(16)) register_14 (.D(WriteData), .en(and_14_out), .Q(register_14_q), .clk(in_8));  // open: clr
  Register #(.width(16)) register_15 (.D(WriteData), .en(and_15_out), .Q(register_15_q), .clk(in_8));  // open: clr
  Register #(.width(16)) register_16 (.D(WriteData), .en(and_16_out), .Q(register_16_q), .clk(in_8));  // open: clr
  Multiplexer #(.width(16)) multiplexer_1 (
    .in0(WriteData), .in1(register_17_q), .out(multiplexer_1_out), .sel(inclk));  // open: en
  Register #(.width(16)) register_17 (.D(in), .Q(register_17_q), .clk(inclk));  // open: en, clr
  Multiplexer #(.select(4), .width(16)) multiplexer_2 (
    .in0(register_1_q), .in1(register_2_q), .in2(register_3_q), .in3(register_4_q), .in4(register_5_q),
    .in5(register_6_q), .in6(register_7_q), .in7(register_8_q), .in8(register_9_q), .in9(register_10_q),
    .in10(register_11_q), .in11(register_12_q), .in12(register_13_q), .in13(register_14_q),
    .in14(register_15_q), .in15(register_16_q), .out(RdReg1), .sel(WriteReg1));  // open: en
  Multiplexer #(.select(4), .width(16)) multiplexer_3 (
    .in0(register_1_q), .in1(register_2_q), .in2(register_3_q), .in3(register_4_q), .in4(register_5_q),
    .in5(register_6_q), .in6(register_7_q), .in7(register_8_q), .in8(register_9_q), .in9(register_10_q),
    .in10(register_11_q), .in11(register_12_q), .in12(register_13_q), .in13(register_14_q),
    .in14(register_15_q), .in15(register_16_q), .out(RdReg2), .sel(WriteReg2));  // open: en
endmodule

module Lab5Register (
  input  [15:0] in_1,
  input  [3:0] in_2,
  input  [3:0] in_3,
  input  [3:0] in_4,
  input  in_5,
  input  [15:0] in_6,
  output [15:0] out_7,
  output [15:0] out_8
);

  wire clock_1_out;

  Clock clock_1 (.out(clock_1_out));
  main main_1 (
    .WriteData(in_1), .RdReg(in_2), .in_8(clock_1_out), .WriteReg1(in_3), .WriteReg2(in_4), .RdReg1(out_7),
    .RdReg2(out_8), .in(in_6), .inclk(in_5));  // open: RegWrite
endmodule
