// Logisim project Parinda Rahman_1931804042.circ as structural Verilog
module Problem_1 (
  input  in_1,
  input  A0,
  input  b0,
  input  A1,
  input  b1,
  input  [1:0] in_6,
  input  in_7,
  input  b2,
  input  a3,
  input  b3,
  output out_11,
  output D1,
  output D2,
  output D3,
  output Cout
);

  wire adder_1_cout, adder_2_cout, adder_3_cout, multiplexer_1_out, multiplexer_2_out, multiplexer_3_out,
       multiplexer_4_out, not_1_out, not_2_out, not_3_out, not_4_out;

  not not_1 (not_1_out, b0);
  not not_2 (not_2_out, b1);
  not not_3 (not_3_out, b2);
  not not_4 (not_4_out, b3);
  Multiplexer #(.select(2)) multiplexer_1 (
    .in0(1'b1), .in1(not_1_out), .in2(b0), .in3(1'b0), .out(multiplexer_1_out), .sel(in_6));  // open: en
  Multiplexer #(.select(2)) multiplexer_2 (
    .in0(1'b1), .in1(not_2_out), .in2(b1), .in3(1'b0), .out(multiplexer_2_out), .sel(in_6));  // open: en
  Multiplexer #(.select(2)) multiplexer_3 (
    .in0(1'b1), .in1(not_3_out), .in2(b2), .in3(1'b0), .out(multiplexer_3_out), .sel(in_6));  // open: en
  Multiplexer #(.select(2)) multiplexer_4 (
    .in0(1'b1), .in1(not_4_out), .in2(b3), .in3(1'b0), .out(multiplexer_4_out), .sel(in_6));  // open: en
  Adder #(.width(1)) adder_1 (.a(A0), .b(multiplexer_1_out), .out(out_11), .cin(in_1), .cout(adder_1_cout));
  Adder #(.width(1)) adder_2 (.a(A1), .b(multiplexer_2_out), .out(D1), .cin(adder_1_cout), .cout(adder_2_cout));
  Adder #(.width(1)) adder_3 (.a(in_7), .b(multiplexer_3_out), .out(D2), .cin(adder_2_cout), .cout(adder_3_cout));
  Adder #(.width(1)) adder_4 (.a(a3), .b(multiplexer_4_out), .out(D3), .cin(adder_3_cout), .cout(Cout));

  // Notes on the sheet:
  //   a2
  //   Cin
  //   D0
endmodule

module Problem_2 (
  input  i5,
  input  shift_right,
  input  i4,
  input  i3,
  input  i2,
  input  i1,
  input  shift_left,
  input  [1:0] in_8,
  input  in_9,
  output A5,
  output A4,
  output A3,
  output A2,
  output A1
);

  wire clock_1_out, multiplexer_1_out, multiplexer_2_out, multiplexer_3_out, multiplexer_4_out,
       multiplexer_5_out;

  Multiplexer #(.select(2)) multiplexer_1 (
    .in0(i1), .in1(A1), .in2(A2), .in3(shift_left), .out(multiplexer_1_out), .sel(in_8));  // open: en
  Multiplexer #(.select(2)) multiplexer_2 (
    .in0(i5), .in1(A5), .in2(shift_right), .in3(A4), .out(multiplexer_2_out), .sel(in_8));  // open: en
  Multiplexer #(.select(2)) multiplexer_3 (
    .in0(i4), .in1(A4), .in2(A5), .in3(A3), .out(multiplexer_3_out), .sel(in_8));  // open: en
  Multiplexer #(.select(2)) multiplexer_4 (
    .in0(i3), .in1(A3), .in2(A4), .in3(A2), .out(multiplexer_4_out), .sel(in_8));  // open: en
  Multiplexer #(.select(2)) multiplexer_5 (
    .in0(i2), .in1(A2), .in2(A3), .in3(A1), .out(multiplexer_5_out), .sel(in_8));  // open: en
  Clock clock_1 (.out(clock_1_out));
  D_Flip_Flop d_ff_1 (.clk(clock_1_out), .D(multiplexer_2_out), .Q(A5), .reset(in_9));  // open: Qn, preset, en
  D_Flip_Flop d_ff_2 (.clk(clock_1_out), .D(multiplexer_3_out), .Q(A4), .reset(in_9));  // open: Qn, preset, en
  D_Flip_Flop d_ff_3 (.clk(clock_1_out), .D(multiplexer_4_out), .Q(A3), .reset(in_9));  // open: Qn, preset, en
  D_Flip_Flop d_ff_4 (.clk(clock_1_out), .D(multiplexer_5_out), .Q(A2), .reset(in_9));  // open: Qn, preset, en
  D_Flip_Flop d_ff_5 (.clk(clock_1_out), .D(multiplexer_1_out), .Q(A1));  // open: Qn, preset, en, reset

  // Notes on the sheet:
  //   S1 S0
  //   1931804042
  //   PARINDA RAHMAN
endmodule
