// Logisim project Project pt1.circ as structural Verilog: 1 circuit, main circuit main
module main (
  input  A,
  input  B,
  input  C,
  input  D
);

  wire and_1_out, and_2_out, and_3_out, and_4_out, and_5_out, and_6_out, and_7_out, and_8_out, and_9_out,
       and_10_out, and_11_out, and_12_out, and_13_out, and_14_out, and_15_out, and_16_out, and_17_out,
       and_18_out, not_1_out, not_2_out, not_3_out, not_4_out, or_1_out, or_2_out, or_3_out, or_4_out,
       or_5_out, or_6_out, or_7_out, undriven;

  not not_1 (not_1_out, A);
  not not_2 (not_2_out, B);
  not not_3 (not_3_out, C);
  not not_4 (not_4_out, D);
  and and_1 (and_1_out, B, D);
  and and_2 (and_2_out, not_4_out, not_2_out, C);
  and and_3 (and_3_out, D, not_3_out);
  and and_4 (and_4_out, B, not_3_out);
  or or_1 (or_1_out, not_1_out, not_3_out);
  and and_5 (and_5_out, not_3_out, not_4_out);
  and and_6 (and_6_out, not_4_out, not_2_out, C);
  and and_7 (and_7_out, not_3_out, B);
  and and_8 (and_8_out, B, D);
  and and_9 (and_9_out, not_3_out, D);
  and and_10 (and_10_out, D, B);
  and and_11 (and_11_out, B, not_3_out);
  and and_12 (and_12_out, A, D);
  and and_13 (and_13_out, not_3_out, not_1_out, D);
  and and_14 (and_14_out, A, not_4_out);
  or or_2 (or_2_out, and_1_out, and_2_out, and_3_out, and_4_out);
  or or_3 (or_3_out, and_5_out, not_1_out);
  or or_4 (or_4_out, and_6_out, and_7_out, and_8_out, and_9_out);
  or or_5 (or_5_out, and_10_out, and_11_out, and_12_out);
  or or_6 (or_6_out, and_13_out, B, and_14_out);
  _7_Segment_Display u_7_segment_display_1 (
    .g(or_7_out), .f(or_6_out), .a(or_2_out), .b(or_1_out), .e(or_5_out), .d(or_4_out), .c(or_3_out),
    .dp(undriven));
  and and_15 (and_15_out, not_2_out, not_3_out, D);
  and and_16 (and_16_out, A, not_3_out);
  and and_17 (and_17_out, C, not_4_out);
  and and_18 (and_18_out, B, not_4_out);
  or or_7 (or_7_out, and_15_out, and_16_out, and_17_out, and_18_out);

  // Notes on the sheet:
  //   a=BC'+BD+C'D +B'CD'
  //   a
  //   b=A'+C'
  //   c=A'+C'D'
  //   d=C'D+BD+BC'+CD'B'
  //   e=BD+BC'+AD
  //   b
  //   a
  //   f
  //   g
  //   dot
  //   c
  //   d
  //   e
  //   f=B+AD'+C'A'D
  //   Parinda Rahman 
  //   1931804042
  //   g=AC'+CD'+BD'+B'C'D
endmodule
