// Logisim project Project pt2.circ as structural Verilog: 1 circuit, main circuit main
module main (
  input  A,
  input  B,
  input  C,
  input  D
);

  wire nand_1_out, nand_2_out, nand_3_out, nand_4_out, nand_5_out, nand_6_out, nand_7_out, nand_8_out,
       nand_9_out, nand_10_out, nand_11_out, nand_12_out, nand_13_out, nand_14_out, nand_15_out, nand_16_out,
       nand_17_out, nand_18_out, nand_19_out, nand_20_out, nand_21_out, nand_22_out, nand_23_out,
       nand_24_out, nand_25_out, nand_26_out, nand_27_out, nand_28_out, nand_29_out, nand_30_out,
       nand_31_out, nand_32_out, nand_33_out, nand_34_out, nand_35_out, nand_36_out, nand_37_out,
       nand_38_out, nand_39_out, nand_40_out, nor_1_out, nor_2_out, nor_3_out, nor_4_out, nor_5_out,
       nor_6_out, nor_7_out, nor_8_out, nor_9_out, nor_10_out, nor_11_out, nor_12_out, nor_13_out,
       nor_14_out, undriven;

  nand nand_1 (nand_1_out, A, A);
  nand nand_2 (nand_2_out, B, B);
  nand nand_3 (nand_3_out, C, C);
  nand nand_4 (nand_4_out, D, D);
  nor nor_1 (nor_1_out, nand_1_out, nand_3_out);
  nand nand_5 (nand_5_out, nand_3_out, nand_4_out);
  nand nand_6 (nand_6_out, B, nand_3_out);
  nand nand_7 (nand_7_out, B, D);
  nand nand_8 (nand_8_out, nand_3_out, D);
  nand nand_9 (nand_9_out, nand_2_out, C, nand_4_out);
  nor nor_2 (nor_2_out, nor_1_out, nor_1_out);
  nand nand_10 (nand_10_out, nand_5_out, nand_5_out);
  nand nand_11 (nand_11_out, D, nand_3_out);
  nand nand_12 (nand_12_out, B, D);
  nand nand_13 (nand_13_out, B, nand_3_out);
  nand nand_14 (nand_14_out, nand_4_out, nand_2_out, C);
  nand nand_15 (nand_15_out, B, D);
  nand nand_16 (nand_16_out, B, nand_3_out);
  nand nand_17 (nand_17_out, A, D);
  nand nand_18 (nand_18_out, A, nand_4_out);
  nand nand_19 (nand_19_out, nand_1_out, nand_3_out, D);
  nand nand_20 (nand_20_out, A, nand_3_out);
  nand nand_21 (nand_21_out, C, nand_4_out);
  nand nand_22 (nand_22_out, B, nand_4_out);
  nand nand_23 (nand_23_out, nand_2_out, nand_3_out, D);
  nand nand_24 (nand_24_out, nand_6_out, nand_6_out);
  nand nand_25 (nand_25_out, nand_7_out, nand_7_out);
  nand nand_26 (nand_26_out, nand_8_out, nand_8_out);
  nand nand_27 (nand_27_out, nand_9_out, nand_9_out);
  nor nor_3 (nor_3_out, nand_10_out, nand_1_out);
  nand nand_28 (nand_28_out, nand_11_out, nand_11_out);
  nand nand_29 (nand_29_out, nand_12_out, nand_12_out);
  nand nand_30 (nand_30_out, nand_13_out, nand_13_out);
  nand nand_31 (nand_31_out, nand_14_out, nand_14_out);
  nand nand_32 (nand_32_out, nand_15_out, nand_15_out);
  nand nand_33 (nand_33_out, nand_16_out, nand_16_out);
  nand nand_34 (nand_34_out, nand_17_out, nand_17_out);
  nand nand_35 (nand_35_out, nand_18_out, nand_18_out);
  nand nand_36 (nand_36_out, nand_19_out, nand_19_out);
  nand nand_37 (nand_37_out, nand_20_out, nand_20_out);
  nand nand_38 (nand_38_out, nand_21_out, nand_21_out);
  nand nand_39 (nand_39_out, nand_22_out, nand_22_out);
  nand nand_40 (nand_40_out, nand_23_out, nand_23_out);
  nor nor_4 (nor_4_out, nor_3_out, nor_3_out);
  nor nor_5 (nor_5_out, nand_24_out, nand_25_out, nand_26_out, nand_27_out);
  nor nor_6 (nor_6_out, nand_28_out, nand_29_out, nand_30_out, nand_31_out);
  nor nor_7 (nor_7_out, nand_32_out, nand_33_out, nand_34_out);
  nor nor_8 (nor_8_out, nand_35_out, nand_36_out, B);
  nor nor_9 (nor_9_out, nand_37_out, nand_38_out, nand_39_out, nand_40_out);
  nor nor_10 (nor_10_out, nor_5_out, nor_5_out);
  nor nor_11 (nor_11_out, nor_6_out, nor_6_out);
  nor nor_12 (nor_12_out, nor_7_out, nor_7_out);
  nor nor_13 (nor_13_out, nor_8_out, nor_8_out);
  nor nor_14 (nor_14_out, nor_9_out, nor_9_out);
  _7_Segment_Display u_7_segment_display_1 (
    .g(nor_14_out), .f(nor_13_out), .a(nor_10_out), .b(nor_2_out), .e(nor_12_out), .d(nor_11_out),
    .c(nor_4_out), .dp(undriven));

  // Notes on the sheet:
  //   g
  //   c
  //   e
  //   1931804042
  //   b
  //   a
  //   f
  //   dot
  //   c
  //   d
  //   Parinda Rahman 
endmodule
