// Logisim project Project pt3.circ as structural Verilog: 1 circuit, main circuit main
module main (
  input  [3:0] in_1
);

  wire decoder_1_out0, decoder_1_out1, decoder_1_out2, decoder_1_out3, decoder_1_out4, decoder_1_out5,
       decoder_1_out6, decoder_1_out7, decoder_1_out8, decoder_1_out9, or_1_out, or_2_out, or_3_out,
       or_4_out, or_5_out, or_6_out, or_7_out, undriven;

  Decoder #(.select(4)) decoder_1 (
    .out0(decoder_1_out0), .out1(decoder_1_out1), .out2(decoder_1_out2), .out3(decoder_1_out3),
    .out4(decoder_1_out4), .out5(decoder_1_out5), .out6(decoder_1_out6), .out7(decoder_1_out7),
    .out8(decoder_1_out8), .out9(decoder_1_out9), .sel(in_1));  // open: out10, out11, out12, out13, out14, out15, en
  or or_1 (or_1_out, decoder_1_out1, decoder_1_out2, decoder_1_out4, decoder_1_out5, decoder_1_out7, decoder_1_out9);
  or or_2 (or_2_out, decoder_1_out0, decoder_1_out1, decoder_1_out2, decoder_1_out3, decoder_1_out4, decoder_1_out5, decoder_1_out6, decoder_1_out7, decoder_1_out8, decoder_1_out9);
  or or_3 (or_3_out, decoder_1_out0, decoder_1_out1, decoder_1_out2, decoder_1_out3, decoder_1_out4, decoder_1_out5, decoder_1_out6, decoder_1_out7, decoder_1_out8);
  or or_4 (or_4_out, decoder_1_out1, decoder_1_out2, decoder_1_out4, decoder_1_out5, decoder_1_out7, decoder_1_out9);
  or or_5 (or_5_out, decoder_1_out4, decoder_1_out5, decoder_1_out7, decoder_1_out9);
  or or_6 (or_6_out, decoder_1_out1, decoder_1_out4, decoder_1_out5, decoder_1_out6, decoder_1_out7, decoder_1_out8);
  or or_7 (or_7_out, decoder_1_out1, decoder_1_out2, decoder_1_out4, decoder_1_out6, decoder_1_out8, decoder_1_out9);
  _7_Segment_Display u_7_segment_display_1 (
    .g(or_7_out), .f(or_6_out), .a(or_1_out), .b(or_2_out), .e(or_5_out), .d(or_4_out), .c(or_3_out),
    .dp(undriven));

  // Notes on the sheet:
  //   4X16
  //   a=1,2,4,5,7,9
  //   b=0,1,2,3,4,5,6,7,8,9
  //   c=0,1,2,3,4,5,6,7,8,
  //   d=1,2,4,5,7,9
  //   e=4,5,7,9
  //   f=1,4,5,6,7,8
  //   g=1,2,4,6,8,9
  //   a
  //   f
  //   g
  //   d
  //   e
  //   b
  //   dot
  //   c
  //   2
  //   3
  //   4
  //   5
  //   6
  //   7
  //   8
  //   9
  //   0
  //   1
  //   1931804042
  //   DECODER
  //   Parinda Rahman 
endmodule
