// Logisim project Project pt4 with counter.circ as structural Verilog: 1 circuit, main circuit main
module main (
  input  in_1,
  input  in_2,
  output D,
  output out_4,
  output out_5,
  output out_6,
  output [2:0] A
);

  wire and_1_out, and_2_out, and_3_out, and_4_out, clock_1_out, multiplexer_1_out, multiplexer_2_out,
       multiplexer_3_out, multiplexer_4_out, multiplexer_5_out, multiplexer_6_out, multiplexer_7_out,
       not_1_out, or_1_out, t_ff_1_qn, undriven, undriven_2, undriven_3;

  not not_1 (not_1_out, D);
  Multiplexer #(.select(3)) multiplexer_1 (
    .in0(in_1), .in1(D), .in2(in_1), .in3(in_1), .in4(not_1_out), .in5(not_1_out), .in6(in_1),
    .in7(not_1_out), .out(multiplexer_1_out), .sel(A));  // open: en
  Multiplexer #(.select(3)) multiplexer_2 (
    .in0(D), .in1(not_1_out), .in2(in_1), .in3(in_1), .in4(not_1_out), .in5(not_1_out), .in6(not_1_out),
    .in7(not_1_out), .out(multiplexer_2_out), .sel(A));  // open: en
  Multiplexer #(.select(3)) multiplexer_3 (
    .in0(in_1), .in1(1'b1), .in2(not_1_out), .in3(in_1), .in4(not_1_out), .in5(not_1_out), .in6(in_1),
    .in7(not_1_out), .out(multiplexer_3_out), .sel(A));  // open: en
  Multiplexer #(.select(3)) multiplexer_4 (
    .in0(1'b1), .in1(not_1_out), .in2(not_1_out), .in3(not_1_out), .in4(not_1_out), .in5(not_1_out),
    .in6(not_1_out), .in7(not_1_out), .out(multiplexer_4_out), .sel(A));  // open: en
  Multiplexer #(.select(3)) multiplexer_5 (
    .in0(in_1), .in1(1'b1), .in2(not_1_out), .in3(in_1), .in4(not_1_out), .in5(not_1_out), .in6(in_1),
    .in7(not_1_out), .out(multiplexer_5_out), .sel(A));  // open: en
  Multiplexer #(.select(3)) multiplexer_6 (
    .in0(1'b1), .in1(1'b1), .in2(not_1_out), .in3(not_1_out), .in4(not_1_out), .in5(not_1_out),
    .in6(not_1_out), .in7(not_1_out), .out(multiplexer_6_out), .sel(A), .en(undriven));
  _7_Segment_Display u_7_segment_display_1 (
    .g(multiplexer_7_out), .f(multiplexer_2_out), .a(multiplexer_3_out), .b(multiplexer_6_out),
    .e(multiplexer_1_out), .d(multiplexer_5_out), .c(multiplexer_4_out), .dp(undriven_2));
  Multiplexer #(.select(3)) multiplexer_7 (
    .in0(D), .in1(1'b1), .in2(not_1_out), .in3(in_2), .in4(not_1_out), .in5(in_2), .in6(not_1_out),
    .in7(in_2), .out(multiplexer_7_out), .sel(A));  // open: en
  Clock clock_1 (.out(clock_1_out));
  and and_1 (and_1_out, A[0], A[1], A[2]);
  and and_2 (and_2_out, A[0], D);
  or or_1 (or_1_out, and_1_out, and_2_out);
  and and_3 (and_3_out, A[1], A[0]);
  and and_4 (and_4_out, t_ff_1_qn, A[0]);
  T_Flip_Flop t_ff_1 (.clk(clock_1_out), .T(or_1_out), .Q(D), .Qn(t_ff_1_qn));  // open: preset, reset, en
  T_Flip_Flop t_ff_2 (.clk(clock_1_out), .T(and_3_out), .Q(A[2]));  // open: Qn, preset, reset, en
  T_Flip_Flop t_ff_3 (.clk(clock_1_out), .T(and_4_out), .Q(A[1]));  // open: Qn, preset, reset, en
  T_Flip_Flop t_ff_4 (.clk(clock_1_out), .T(1'b1), .Q(A[0]), .preset(undriven_3));  // open: Qn, reset, en

  assign out_4 = A[2];
  assign out_5 = A[1];
  assign out_6 = A[0];

  // Notes on the sheet:
  //   D
  //   I1
  //   I0
  //   I2
  //   I3
  //   I4
  //   I5
  //   I6
  //   I7
  //   B
  //   C
  //   g
  //   e
  //   b
  //   a
  //   f
  //   dot
  //   c
  //   d
  //   Parinda Rahman 
  //   1931804042
  //   MUX
  //   D
  //   D'
  //   C
  //   C'
  //   B
  //   B'
  //   A
  //   A'
  //   C
  //   B
  //   A
endmodule
