// Logisim project cse332 lab6.circ as structural Verilog: 1 circuit, main circuit main
module main (
  input  A,
  input  B,
  input  cin,
  input  [1:0] in_4,
  output Result,
  output Carry_out
);

  wire adder_1_out, and_1_out, multiplexer_1_out, multiplexer_2_out, not_1_out, or_1_out;

  Multiplexer multiplexer_1 (.in0(cin), .in1(1'b1), .out(multiplexer_1_out), .sel(in_4[0]));  // open: en
  not not_1 (not_1_out, B);
  Multiplexer multiplexer_2 (.in0(B), .in1(not_1_out), .out(multiplexer_2_out), .sel(in_4[0]));  // open: en
  and and_1 (and_1_out, A, B);
  or or_1 (or_1_out, B, A);
  Adder #(.width(1)) adder_1 (
    .a(A), .b(multiplexer_2_out), .out(adder_1_out), .cin(multiplexer_1_out), .cout(Carry_out));
  Multiplexer #(.select(2)) multiplexer_3 (
    .in0(and_1_out), .in1(or_1_out), .in2(adder_1_out), .in3(adder_1_out), .out(Result), .sel(in_4));  // open: en

  // Other names for the same wires on the sheet: s0 = in_4[0]

  // Notes on the sheet:
  //   00 and,01 or, 10 add,11 sub
endmodule
