// Logisim project finals.circ as structural Verilog: 1 circuit, main circuit main
module main (
  output A,
  output out_2,
  output C,
  output D_Z_prime
);

  wire and_1_out, and_2_out, and_3_out, and_4_out, and_5_out, and_6_out, and_7_out, and_8_out, and_9_out,
       clock_1_out, or_1_out, or_2_out, t_ff_1_q, t_ff_1_qn, t_ff_2_q, t_ff_2_qn, t_ff_3_q, t_ff_3_qn;

  Clock clock_1 (.out(clock_1_out));
  and and_1 (and_1_out, t_ff_3_q, t_ff_3_q);
  or or_1 (or_1_out, t_ff_1_q, and_1_out, t_ff_2_q);
  or or_2 (or_2_out, and_2_out, and_3_out);
  and and_2 (and_2_out, t_ff_3_qn, t_ff_1_qn);
  and and_3 (and_3_out, t_ff_3_q, D_Z_prime);
  T_Flip_Flop t_ff_1 (.clk(clock_1_out), .T(or_1_out), .Q(t_ff_1_q), .Qn(t_ff_1_qn));  // open: preset, reset, en
  T_Flip_Flop t_ff_2 (.clk(clock_1_out), .T(or_2_out), .Q(t_ff_2_q), .Qn(t_ff_2_qn));  // open: preset, reset, en
  T_Flip_Flop t_ff_3 (.clk(clock_1_out), .T(t_ff_3_q), .Q(t_ff_3_q), .Qn(t_ff_3_qn));  // open: preset, reset, en
  T_Flip_Flop t_ff_4 (.clk(clock_1_out), .T(1'b1), .Q(t_ff_3_q), .Qn(D_Z_prime));  // open: preset, reset, en
  and and_4 (and_4_out, t_ff_3_q, t_ff_3_q);
  or or_3 (A, t_ff_2_q, t_ff_1_q, and_4_out);
  and and_5 (and_5_out, t_ff_1_qn, t_ff_2_qn, D_Z_prime);
  and and_6 (and_6_out, t_ff_2_q, t_ff_3_q, t_ff_3_q);
  and and_7 (and_7_out, t_ff_2_qn, t_ff_3_qn);
  and and_8 (and_8_out, t_ff_3_qn, t_ff_3_q);
  and and_9 (and_9_out, t_ff_3_q, D_Z_prime);
  or or_4 (out_2, and_5_out, and_6_out, and_7_out);
  or or_5 (C, and_8_out, and_9_out);

  // Notes on the sheet:
  //   Tz
  //   Tw
  //   Tx
  //   Ty
  //   w
  //   W'
  //   X
  //   X'
  //   Y
  //   Y'
  //   Z
  //   Z'
  //   A=X+Y+YZ
  //   B=Y'X'+XZY+X'Y'Z'
  //   C=Y'Z+YZ'
  //   D
  //   B
  //   1931804042
  //   Parinda Rahman 
  //   Parinda Rahman 
  //   1931804042
endmodule
