// Logisim project lab 6actual 1.circ as structural Verilog: 1 circuit, main circuit main
module main (
  input  I0,
  input  i1,
  input  I2,
  input  I3,
  input  in_5,
  input  S0,
  output out_7
);

  wire and_1_out, and_2_out, and_3_out, and_4_out, not_1_out, not_2_out, or_1_out, or_2_out;

  not not_1 (not_1_out, in_5);
  not not_2 (not_2_out, S0);
  and and_1 (and_1_out, I0, not_1_out, not_2_out);
  and and_2 (and_2_out, i1, not_1_out, S0);
  and and_3 (and_3_out, I2, in_5, not_2_out);
  and and_4 (and_4_out, I3, in_5, S0);
  or or_1 (or_1_out, and_1_out, and_2_out);
  or or_2 (or_2_out, and_3_out, and_4_out);
  or or_3 (out_7, or_1_out, or_2_out);

  // Notes on the sheet:
  //   S1
  //   1931804042
  //   Parinda Rahman 
endmodule
