// Logisim project lab4 nor.circ as structural Verilog: 1 circuit, main circuit main
module main (
  input  W,
  input  X,
  input  Y,
  input  Z,
  output A,
  output B,
  output C,
  output D
);

  wire nor_1_out, nor_2_out, nor_3_out, nor_5_out, nor_6_out, nor_7_out, nor_8_out, nor_9_out, nor_10_out,
       nor_11_out, nor_12_out, nor_13_out, nor_14_out, nor_15_out, nor_16_out, nor_17_out, nor_18_out,
       nor_19_out, nor_20_out, nor_21_out, nor_22_out, nor_23_out, nor_24_out, nor_25_out, nor_26_out,
       nor_27_out, nor_28_out, nor_31_out, nor_32_out;

  nor nor_1 (nor_1_out, W, W);
  nor nor_2 (nor_2_out, X, X);
  nor nor_3 (nor_3_out, Y, Y);
  nor nor_4 (D, Z, Z);
  nor nor_5 (nor_5_out, W, W);
  nor nor_6 (nor_6_out, Y, Y);
  nor nor_7 (nor_7_out, D, D);
  nor nor_8 (nor_8_out, X, X);
  nor nor_9 (nor_9_out, W, W);
  nor nor_10 (nor_10_out, Y, Y);
  nor nor_11 (nor_11_out, Z, Z);
  nor nor_12 (nor_12_out, nor_2_out, nor_2_out);
  nor nor_13 (nor_13_out, D, D);
  nor nor_14 (nor_14_out, X, X);
  nor nor_15 (nor_15_out, nor_3_out, nor_3_out);
  nor nor_16 (nor_16_out, Z, Z);
  nor nor_17 (nor_17_out, nor_6_out, nor_7_out);
  nor nor_18 (nor_18_out, nor_5_out, nor_8_out);
  nor nor_19 (nor_19_out, nor_9_out, nor_10_out, nor_11_out);
  nor nor_20 (nor_20_out, nor_2_out, nor_2_out);
  nor nor_21 (nor_21_out, nor_3_out, nor_3_out);
  nor nor_22 (nor_22_out, nor_12_out, nor_13_out);
  nor nor_23 (nor_23_out, Z, Z);
  nor nor_24 (nor_24_out, nor_15_out, nor_16_out);
  nor nor_25 (nor_25_out, nor_18_out, nor_19_out);
  nor nor_26 (nor_26_out, nor_20_out, nor_21_out);
  nor nor_27 (nor_27_out, Y, Y);
  nor nor_28 (nor_28_out, nor_24_out, nor_17_out);
  nor nor_29 (A, nor_25_out, nor_25_out);
  nor nor_30 (C, nor_28_out, nor_28_out);
  nor nor_31 (nor_31_out, nor_14_out, nor_27_out, nor_23_out);
  nor nor_32 (nor_32_out, nor_26_out, nor_22_out, nor_31_out);
  nor nor_33 (B, nor_32_out, nor_32_out);

  // Notes on the sheet:
  //   WX
  //   YZ'
  //   WYZ
  //   Y'Z
  //   X'Z'
  //   XYZ
  //   WX+WYZ
  //   X'Y'
  //   Z'
  //   Y'Z+YZ'
  //   X'Y'+X'Z'+XYZ
  //   X'Y'+X'Z'+XYZ
  //   PARINDA RAHMAN-1931804042
endmodule
