// Logisim project lab6 2.circ as structural Verilog: 1 circuit, main circuit main
module main (
  input  A,
  input  B,
  input  C,
  input  D
);

  wire and_1_out, and_2_out, and_3_out, and_4_out, and_5_out, and_6_out, and_7_out, and_8_out, and_9_out,
       and_10_out, and_11_out, and_12_out, and_13_out, and_14_out, and_15_out, and_16_out, not_1_out,
       not_2_out, not_3_out, not_4_out, or_1_out, or_2_out, or_3_out, or_4_out, or_5_out, or_6_out, or_7_out,
       undriven;

  not not_1 (not_1_out, A);
  not not_2 (not_2_out, B);
  not not_3 (not_3_out, C);
  not not_4 (not_4_out, D);
  and and_1 (and_1_out, B, D);
  and and_2 (and_2_out, not_4_out, not_2_out);
  and and_3 (and_3_out, C, D);
  and and_4 (and_4_out, not_4_out, not_3_out);
  or or_1 (or_1_out, not_3_out, D, B);
  and and_5 (and_5_out, B, D);
  and and_6 (and_6_out, not_2_out, C);
  and and_7 (and_7_out, not_2_out, not_4_out);
  and and_8 (and_8_out, C, not_4_out);
  and and_9 (and_9_out, not_2_out, not_4_out);
  and and_10 (and_10_out, C, not_4_out);
  and and_11 (and_11_out, not_3_out, not_4_out);
  and and_12 (and_12_out, B, not_3_out);
  and and_13 (and_13_out, B, not_4_out);
  and and_14 (and_14_out, B, not_3_out);
  and and_15 (and_15_out, C, not_4_out);
  and and_16 (and_16_out, not_2_out, C);
  or or_2 (or_2_out, not_2_out, and_3_out, and_4_out);
  or or_3 (or_3_out, and_9_out, and_10_out);
  or or_4 (or_4_out, A, C, and_1_out, and_2_out);
  or or_5 (or_5_out, and_5_out, and_6_out, and_7_out, and_8_out, A);
  or or_6 (or_6_out, and_11_out, and_12_out, and_13_out, A);
  or or_7 (or_7_out, and_14_out, and_15_out, and_16_out, A);
  _7_Segment_Display u_7_segment_display_1 (
    .g(or_7_out), .f(or_6_out), .a(or_4_out), .b(or_2_out), .e(or_3_out), .d(or_5_out), .c(or_1_out),
    .dp(undriven));

  // Notes on the sheet:
  //   B
  //   D
  //   D'
  //   B'
  //   CD
  //   C'D'
  //   D
  //   CD'
  //   a=
  //   A
  //   C
  //   B'
  //   C'
  //   c=C'+D+B
  //   B
  //   BC'D
  //   B'C
  //   B'D'
  //   CD'
  //   A
  //   B'D'
  //   C'D'
  //   BC'
  //   BD'
  //   A
  //   CD'
  //   A+C+BD+B'D'
  //   a
  //   b=B'+CD+C'D'
  //   b
  //   e=B'D'+CD'
  //   BC'
  //   B'C
  //   A
  //   d=BC'D+B'C+B'D'+C'D'+A
  //   f=A+C'D'+BC'+BD'
  //   g=A+BC'+CD'+B'C
  //   Parinda Rahman-1931804042
  //   a
  //   b
  //   f
  //   g
  //   dot
  //   e
  //   d
  //   c
endmodule
