// Logisim project lab6 actual 2.circ as structural Verilog: 1 circuit, main circuit main
module main (
  input  I3,
  input  I2,
  input  I4,
  input  I7,
  input  D,
  input  in_6,
  input  [2:0] C,
  output out_8
);

  wire not_1_out, undriven;

  not not_1 (not_1_out, D);
  Multiplexer #(.select(3)) multiplexer_1 (
    .in0(D), .in1(not_1_out), .in2(I3), .in3(I2), .in4(I4), .in5(not_1_out), .in6(I7), .in7(in_6),
    .out(out_8), .sel(C), .en(undriven));

  // Notes on the sheet:
  //   I1
  //   I0
  //   I5
  //   I6
  //   A
  //   B
  //   Parinda Rahman
  //   1931804042
endmodule
