// Logisim project lab8.circ as structural Verilog: 1 circuit, main circuit main
module main (
  output out_1,
  output B,
  output out_3
);

  wire and_1_out, clock_1_out;

  Clock clock_1 (.out(clock_1_out));
  and and_1 (and_1_out, out_3, B);
  J_K_Flip_Flop j_k_ff_1 (.J(and_1_out), .clk(clock_1_out), .K(and_1_out), .Q(out_1));  // open: Qn, preset, en, reset
  J_K_Flip_Flop j_k_ff_2 (.J(out_3), .clk(clock_1_out), .K(out_3), .Q(B));  // open: Qn, preset, en, reset
  J_K_Flip_Flop j_k_ff_3 (.J(1'b1), .clk(clock_1_out), .K(1'b1), .Q(out_3));  // open: Qn, preset, en, reset

  // Notes on the sheet:
  //   BC
  //   C
  //   1
  //   A
  //   A'
  //   B'
  //   C
  //   C'
  //   Parinda Rahman
  //   1931804042
endmodule
