// Logisim project pc.circ as structural Verilog: 1 circuit, main circuit main
module main (
  output [15:0] out_1
);

  wire Clk_out;
  wire [7:0] adder_1_out, register_1_q;

  Clock Clk (.out(Clk_out));
  Register register_1 (.D(adder_1_out), .Q(register_1_q), .clk(Clk_out));  // open: en, clr
  Adder adder_1 (.a(8'h1), .b(register_1_q), .out(adder_1_out));  // open: cin, cout
  ROM #(.dataWidth(16)) rom_1 (.addr(register_1_q), .data(out_1));  // open: sel
endmodule
