// Logisim project project pt1 with counter.circ as structural Verilog: 1 circuit, main circuit main
module main (
  output D,
  output out_2,
  output out_3,
  output out_4
);

  wire and_1_out, and_2_out, and_3_out, and_4_out, and_5_out, and_6_out, and_7_out, and_8_out, and_9_out,
       and_10_out, and_11_out, and_12_out, and_13_out, and_14_out, and_15_out, and_16_out, and_17_out,
       and_18_out, and_19_out, and_20_out, and_21_out, and_22_out, clock_1_out, not_1_out, not_2_out,
       not_3_out, not_4_out, or_1_out, or_2_out, or_3_out, or_4_out, or_5_out, or_6_out, or_7_out, or_8_out,
       t_ff_1_qn, undriven, undriven_2;

  not not_1 (not_1_out, D);
  not not_2 (not_2_out, out_2);
  not not_3 (not_3_out, out_3);
  not not_4 (not_4_out, out_4);
  and and_1 (and_1_out, out_2, out_4);
  and and_2 (and_2_out, not_4_out, not_2_out, out_3);
  and and_3 (and_3_out, out_4, not_3_out);
  and and_4 (and_4_out, out_2, not_3_out);
  or or_1 (or_1_out, not_1_out, not_3_out);
  and and_5 (and_5_out, not_3_out, not_4_out);
  and and_6 (and_6_out, not_4_out, not_2_out, out_3);
  and and_7 (and_7_out, not_3_out, out_2);
  and and_8 (and_8_out, out_2, out_4);
  and and_9 (and_9_out, not_3_out, out_4);
  and and_10 (and_10_out, out_4, out_2);
  and and_11 (and_11_out, out_2, not_3_out);
  and and_12 (and_12_out, D, out_4);
  and and_13 (and_13_out, not_3_out, not_1_out, out_4);
  and and_14 (and_14_out, D, not_4_out);
  or or_2 (or_2_out, and_1_out, and_2_out, and_3_out, and_4_out);
  or or_3 (or_3_out, and_5_out, not_1_out);
  or or_4 (or_4_out, and_6_out, and_7_out, and_8_out, and_9_out);
  or or_5 (or_5_out, and_10_out, and_11_out, and_12_out);
  or or_6 (or_6_out, and_13_out, out_2, and_14_out);
  _7_Segment_Display u_7_segment_display_1 (
    .g(or_7_out), .f(or_6_out), .a(or_2_out), .b(or_1_out), .e(or_5_out), .d(or_4_out), .c(or_3_out),
    .dp(undriven));
  and and_15 (and_15_out, not_2_out, not_3_out, out_4);
  and and_16 (and_16_out, D, not_3_out);
  and and_17 (and_17_out, out_3, not_4_out);
  and and_18 (and_18_out, out_2, not_4_out);
  Clock clock_1 (.out(clock_1_out));
  or or_7 (or_7_out, and_15_out, and_16_out, and_17_out, and_18_out);
  and and_19 (and_19_out, out_4, out_3, out_2);
  and and_20 (and_20_out, out_4, D);
  or or_8 (or_8_out, and_19_out, and_20_out);
  and and_21 (and_21_out, out_3, out_4);
  and and_22 (and_22_out, t_ff_1_qn, out_4);
  T_Flip_Flop t_ff_1 (.clk(clock_1_out), .T(or_8_out), .Q(D), .Qn(t_ff_1_qn));  // open: preset, reset, en
  T_Flip_Flop t_ff_2 (.clk(clock_1_out), .T(and_21_out), .Q(out_2));  // open: Qn, preset, reset, en
  T_Flip_Flop t_ff_3 (.clk(clock_1_out), .T(and_22_out), .Q(out_3));  // open: Qn, preset, reset, en
  T_Flip_Flop t_ff_4 (.clk(clock_1_out), .T(1'b1), .Q(out_4), .preset(undriven_2));  // open: Qn, reset, en

  // Notes on the sheet:
  //   A
  //   a
  //   b
  //   c
  //   d
  //   e
  //   b
  //   a
  //   f
  //   g
  //   dot
  //   c
  //   d
  //   e
  //   f
  //   g
  //   Parinda Rahman 
  //   1931804042
  //   Combinational circuit with gates 
  //   D
  //   D'
  //   C
  //   C'
  //   B
  //   B'
  //   A
  //   A'
  //   A
  //   C
  //   B
endmodule
