// Logisim project sychrounous counter.circ as structural Verilog: 1 circuit, main circuit main
module main (
  output D,
  output out_2,
  output out_3,
  output out_4
);

  wire and_1_out, and_2_out, and_3_out, and_4_out, clock_1_out, or_1_out, t_ff_1_qn, undriven;

  Clock clock_1 (.out(clock_1_out));
  and and_1 (and_1_out, out_4, out_3, out_2);
  and and_2 (and_2_out, out_4, D);
  or or_1 (or_1_out, and_1_out, and_2_out);
  and and_3 (and_3_out, out_3, out_4);
  and and_4 (and_4_out, t_ff_1_qn, out_4);
  T_Flip_Flop t_ff_1 (.clk(clock_1_out), .T(or_1_out), .Q(D), .Qn(t_ff_1_qn));  // open: preset, reset, en
  T_Flip_Flop t_ff_2 (.clk(clock_1_out), .T(and_3_out), .Q(out_2));  // open: Qn, preset, reset, en
  T_Flip_Flop t_ff_3 (.clk(clock_1_out), .T(and_4_out), .Q(out_3));  // open: Qn, preset, reset, en
  T_Flip_Flop t_ff_4 (.clk(clock_1_out), .T(1'b1), .Q(out_4), .preset(undriven));  // open: Qn, reset, en

  // Notes on the sheet:
  //   Td=AD+ABC
  //   Tb=AD'
  //   Tc=AB
  //   Ta=1
  //   D
  //   D'
  //   C
  //   C'
  //   B
  //   B'
  //   A
  //   A'
  //   A
  //   C
  //   B
endmodule
